# Fritzing sketch bsb9000 (saved by Fritzing 0.9.3b)
breadboards: 1

parts:
  ProMini = Arduino Pro Mini v13
  J1 = AVR ISP 6 Pin [package=2x3_lock]
  DFRobot_DFPlayer_Mini1 = DFRobot DFPlayer Mini [part_number=DFR0299]
  Q1 = Basic FET N-Channel [package="TO220 [THT]"]
  D1 = Rectifier Diode [part_number=1N4001 package="300 mil [THT]"]
  R1 = Resistor [tolerance=±5% resistance=10k package=THT]
  R2 = Resistor [tolerance=±5% resistance=33 package=THT]
  R3 = Resistor [tolerance=±5% resistance=1k package=THT]
  SPKR1 = Loudspeaker [part_number=3W]
  S1 = Pushbutton [package="[THT]"]
  JP1 = Header 6 [package=1x06_smd_straight_alt]
  VCC1 = 4 x AAA Battery Mount
  RGB_SMD_LED1 = SMD RGB LED (WS2812) [package=5050]
  C1 = Electrolytic Capacitor [capacitance=1mF package="100 mil [THT, electrolytic]"]

nets:
  VCC: ProMini.VCC, J1.2, DFRobot_DFPlayer_Mini1.VCC, D1.cathode, JP1.5, VCC1.+, RGB_SMD_LED1.VCC, RGB_SMD_LED1.VDD, C1.+
  N1: ProMini.GND, J1.6, Q1.source, R1.Pin_0, S1.Pin_1, S1.Pin_2, JP1.4, VCC1.-
  N2: ProMini.D13/SCK, J1.3
  N3: ProMini.D12/MISO, J1.1
  N4: ProMini.D11_PWM/MOSI, J1.4
  N5: ProMini.D10_PWM/SS, JP1.3
  N6: ProMini.D9_PWM, JP1.2
  N7: ProMini.D8, JP1.1
  N8: ProMini.D7, R1.Pin_1, R2.Pin_0
  N9: ProMini.D4, RGB_SMD_LED1.DIn
  N10: ProMini.D3_PWM, DFRobot_DFPlayer_Mini1.BUSY
  N11: ProMini.D2, S1.Pin_3, S1.Pin_4
  N12: ProMini.RESET, J1.5
  N13: ProMini.D1/RX, DFRobot_DFPlayer_Mini1.TX
  N14: ProMini.D0/TX, R3.Pin_0
  N15: DFRobot_DFPlayer_Mini1.RX, R3.Pin_1
  N16: DFRobot_DFPlayer_Mini1.SPK_1, SPKR1.pin1
  N17: DFRobot_DFPlayer_Mini1.SPK_2, SPKR1.pin2
  N18: DFRobot_DFPlayer_Mini1.GND-2, Q1.drain, D1.anode, RGB_SMD_LED1.VSS, C1.-
  N19: Q1.gate, R2.Pin_1

notes:
  BSB9000, BSB9000 - Annoying audio button ( https://gitlab.com/krayon/bsb9000 | https://github.com/krayon/bsb9000 ), 0.1
